// Logisim project branch_comp.circ as structural Verilog: 1 circuit, main circuit branch_comp
module branch_comp (
  input  [31:0] rs1,
  input  [31:0] rs2,
  input  BrUn,
  output BrEq,
  output BrLt
);

  wire BrLt_Signed, BrLt_Unsigned;

  Comparator #(.mode("unsigned"), .width(32)) comparator_1 (.a(rs1), .b(rs2), .lt(BrLt_Unsigned));  // open: gt, eq
  Comparator #(.width(32)) comparator_2 (.a(rs1), .b(rs2), .eq(BrEq), .lt(BrLt_Signed));  // open: gt
  Multiplexer #(.enable("false")) multiplexer_1 (.in0(BrLt_Signed), .in1(BrLt_Unsigned), .out(BrLt), .sel(BrUn));

  // Notes on the sheet:
  //   INPUTS to your circuit
  //   DON'T CHANGE THE LOCATIONS OF THE INPUTS AND OUTPUTS!
  //   OUTPUT from your circuit
endmodule
