// Logisim project control_logic.circ as structural Verilog: 1 circuit, main circuit control_logic
module control_logic (
  input  [31:0] inst,
  input  BrEq,
  input  BrLt,
  output PCSel,
  output RegWEn,
  output [2:0] ImmSel,
  output BrUn,
  output ASel,
  output BSel,
  output [3:0] ALUSel,
  output [3:0] MemRW,
  output [1:0] WBSel,
  output CSRSel,
  output CSRWen
);

  wire alu_add, alu_and, alu_bsel, alu_mul, alu_mulh, alu_mulhu, alu_or, alu_sll, alu_slt, alu_sra, alu_srl,
       alu_sub, alu_xor, and_1_out, and_2_out, and_3_out, and_4_out, and_5_out, and_6_out, and_26_out,
       and_27_out, and_28_out, and_29_out, and_30_out, and_31_out, and_46_out, and_47_out, and_48_out,
       and_49_out, and_50_out, and_51_out, comparator_8_eq, comparator_9_eq, comparator_11_eq,
       comparator_12_eq, comparator_13_eq, comparator_14_eq, comparator_15_eq, comparator_16_eq,
       comparator_17_eq, comparator_18_eq, comparator_19_eq, comparator_20_eq, comparator_21_eq,
       comparator_22_eq, comparator_23_eq, comparator_24_eq, comparator_25_eq, comparator_26_eq,
       comparator_27_eq, comparator_28_eq, comparator_29_eq, comparator_30_eq, comparator_31_eq,
       comparator_32_eq, comparator_33_eq, comparator_34_eq, comparator_35_eq, comparator_36_eq,
       comparator_37_eq, comparator_38_eq, comparator_39_eq, comparator_40_eq, comparator_41_eq,
       comparator_42_eq, comparator_43_eq, comparator_44_eq, comparator_45_eq, comparator_46_eq,
       comparator_47_eq, comparator_48_eq, comparator_49_eq, comparator_50_eq, comparator_51_eq,
       comparator_52_eq, comparator_53_eq, comparator_54_eq, comparator_55_eq, comparator_56_eq,
       comparator_57_eq, comparator_58_eq, comparator_59_eq, comparator_60_eq, comparator_61_eq,
       comparator_62_eq, comparator_63_eq, comparator_64_eq, comparator_68_eq, comparator_69_eq,
       comparator_70_eq, comparator_71_eq, comparator_72_eq, comparator_73_eq, comparator_74_eq,
       comparator_75_eq, comparator_76_eq, comparator_77_eq, comparator_78_eq, comparator_79_eq,
       comparator_80_eq, comparator_81_eq, comparator_82_eq, comparator_83_eq, comparator_84_eq,
       comparator_85_eq, comparator_86_eq, I_0x03, I_0x13, I_0x67, I_0x73, I_Type, Inst_add, Inst_addi,
       Inst_and, Inst_andi, Inst_auipc, Inst_beq, Inst_bge, Inst_bgeu, Inst_blt, Inst_bltu, Inst_bne,
       Inst_csrwi, Inst_jal, Inst_jalr, Inst_lb, Inst_lh, Inst_lw, Inst_or, Inst_ori, Inst_sb, Inst_sh,
       Inst_sll, Inst_slli, Inst_slt, Inst_slti, Inst_sra, Inst_srai, Inst_srl, Inst_srli, Inst_sw, Inst_xor,
       Inst_xori, multiplexer_1_out, multiplexer_4_out, multiplexer_8_out, multiplexer_9_out,
       multiplexer_14_out, multiplexer_15_out, multiplexer_18_out, multiplexer_25_out, multiplexer_35_out,
       multiplexer_36_out, multiplexer_37_out, multiplexer_38_out, multiplexer_39_out, multiplexer_40_out,
       not_1_out, not_2_out, not_3_out, R_Type, S_Type, SB_Type, U_Type, UJ_Type;
  wire [1:0] multiplexer_5_out, multiplexer_10_out, multiplexer_12_out, multiplexer_21_out,
       multiplexer_26_out;
  wire [2:0] multiplexer_6_out, multiplexer_11_out, multiplexer_16_out, multiplexer_22_out;
  wire [3:0] multiplexer_3_out, multiplexer_7_out, multiplexer_13_out, multiplexer_17_out,
       multiplexer_23_out, multiplexer_24_out, multiplexer_28_out, multiplexer_31_out, multiplexer_32_out,
       multiplexer_33_out, multiplexer_34_out, multiplexer_41_out, multiplexer_42_out;

  Comparator #(.width(7)) comparator_1 (.a(inst[6:0]), .b(7'b0110011), .eq(R_Type));  // open: gt, lt
  Comparator #(.width(7)) comparator_2 (.a(inst[6:0]), .b(7'b0000011), .eq(I_0x03));  // open: gt, lt
  Comparator #(.width(7)) comparator_3 (.a(inst[6:0]), .b(7'b0010011), .eq(I_0x13));  // open: gt, lt
  Comparator #(.width(7)) comparator_4 (.a(inst[6:0]), .b(7'b1100111), .eq(I_0x67));  // open: gt, lt
  Comparator #(.width(7)) comparator_5 (.a(inst[6:0]), .b(7'b1110011), .eq(I_0x73));  // open: gt, lt
  Comparator #(.width(7)) comparator_6 (.a(inst[6:0]), .b(7'b0100011), .eq(S_Type));  // open: gt, lt
  Comparator #(.width(7)) comparator_7 (.a(inst[6:0]), .b(7'b1100011), .eq(SB_Type));  // open: gt, lt
  Comparator #(.width(7)) comparator_8 (.a(inst[6:0]), .b(7'b0010111), .eq(comparator_8_eq));  // open: gt, lt
  Comparator #(.width(7)) comparator_9 (.a(inst[6:0]), .b(7'b0110111), .eq(comparator_9_eq));  // open: gt, lt
  Comparator #(.width(7)) comparator_10 (.a(inst[6:0]), .b(7'b1101111), .eq(UJ_Type));  // open: gt, lt
  or or_1 (alu_sll, Inst_sll, Inst_slli);
  or or_2 (alu_slt, Inst_slt, Inst_slti);
  or or_3 (U_Type, comparator_8_eq, comparator_9_eq);
  or or_4 (alu_add, Inst_add, Inst_lb, Inst_lh, Inst_lw, Inst_addi, Inst_sb, Inst_sh, Inst_sw, Inst_beq, Inst_bge, Inst_bne, Inst_bltu, Inst_blt, Inst_bgeu, Inst_auipc, Inst_jal, Inst_jalr);
  or or_5 (I_Type, I_0x03, I_0x13, I_0x67, I_0x73);
  or or_6 (alu_and, Inst_and, Inst_andi);
  or or_7 (alu_or, Inst_or, Inst_ori);
  or or_8 (alu_xor, Inst_xor, Inst_xori);
  or or_9 (alu_srl, Inst_srl, Inst_srli);
  or or_10 (alu_sra, Inst_sra, Inst_srai);
  Multiplexer #(.enable("false")) multiplexer_1 (.in0(1'b1), .in1(1'b0), .out(multiplexer_1_out), .sel(R_Type));
  Multiplexer #(.enable("false")) multiplexer_2 (.in0(1'b1), .in1(1'b0), .out(BSel), .sel(R_Type));
  Multiplexer #(.enable("false"), .select(2), .width(4)) multiplexer_3 (
    .in0(4'b0001), .in1(4'b0011), .in2(4'b1111), .in3(4'b0000), .out(multiplexer_3_out), .sel(inst[13:12]));
  Multiplexer #(.enable("false")) multiplexer_4 (.in0(1'b0), .in1(1'b1), .out(multiplexer_4_out), .sel(R_Type));
  Multiplexer #(.enable("false"), .width(2)) multiplexer_5 (
    .in0(2'b00), .in1(2'b01), .out(multiplexer_5_out), .sel(R_Type));
  Multiplexer #(.enable("false"), .width(3)) multiplexer_6 (
    .in0(3'b000), .in1(3'b111), .out(multiplexer_6_out), .sel(I_Type));
  Multiplexer #(.enable("false"), .width(4)) multiplexer_7 (
    .in0(4'b1000), .in1(4'b0000), .out(multiplexer_7_out), .sel(alu_add));
  Multiplexer #(.enable("false")) multiplexer_8 (
    .in0(multiplexer_1_out), .in1(1'b0), .out(multiplexer_8_out), .sel(I_Type));
  Multiplexer #(.enable("false")) multiplexer_9 (
    .in0(multiplexer_4_out), .in1(1'b1), .out(multiplexer_9_out), .sel(I_Type));
  Multiplexer #(.enable("false"), .width(2)) multiplexer_10 (
    .in0(multiplexer_5_out), .in1(2'b10), .out(multiplexer_10_out), .sel(I_0x03));
  Multiplexer #(.enable("false"), .width(3)) multiplexer_11 (
    .in0(multiplexer_6_out), .in1(3'b001), .out(multiplexer_11_out), .sel(S_Type));
  Multiplexer #(.enable("false"), .width(2)) multiplexer_12 (
    .in0(multiplexer_10_out), .in1(2'b01), .out(multiplexer_12_out), .sel(I_0x13));
  Multiplexer #(.enable("false"), .width(4)) multiplexer_13 (
    .in0(multiplexer_7_out), .in1(4'b0001), .out(multiplexer_13_out), .sel(alu_and));
  and and_1 (and_1_out, R_Type, 1'b1);
  Comparator #(.width(3)) comparator_11 (.a(inst[14:12]), .b(3'b000), .eq(comparator_11_eq));  // open: gt, lt
  Comparator #(.width(7)) comparator_12 (.a(inst[31:25]), .b({7{1'b0}}), .eq(comparator_12_eq));  // open: gt, lt
  and and_2 (and_2_out, R_Type, 1'b1);
  Comparator #(.width(3)) comparator_13 (.a(inst[14:12]), .b(3'b111), .eq(comparator_13_eq));  // open: gt, lt
  Comparator #(.width(7)) comparator_14 (.a(inst[31:25]), .b({7{1'b0}}), .eq(comparator_14_eq));  // open: gt, lt
  and and_3 (and_3_out, R_Type, 1'b1);
  Comparator #(.width(3)) comparator_15 (.a(inst[14:12]), .b(3'b110), .eq(comparator_15_eq));  // open: gt, lt
  Comparator #(.width(7)) comparator_16 (.a(inst[31:25]), .b({7{1'b0}}), .eq(comparator_16_eq));  // open: gt, lt
  and and_4 (and_4_out, R_Type, 1'b1);
  Comparator #(.width(3)) comparator_17 (.a(inst[14:12]), .b(3'b100), .eq(comparator_17_eq));  // open: gt, lt
  Comparator #(.width(7)) comparator_18 (.a(inst[31:25]), .b({7{1'b0}}), .eq(comparator_18_eq));  // open: gt, lt
  and and_5 (and_5_out, R_Type, 1'b1);
  Comparator #(.width(3)) comparator_19 (.a(inst[14:12]), .b(3'b101), .eq(comparator_19_eq));  // open: gt, lt
  Comparator #(.width(7)) comparator_20 (.a(inst[31:25]), .b({7{1'b0}}), .eq(comparator_20_eq));  // open: gt, lt
  and and_6 (and_6_out, R_Type, 1'b1);
  Comparator #(.width(3)) comparator_21 (.a(inst[14:12]), .b(3'b101), .eq(comparator_21_eq));  // open: gt, lt
  Comparator #(.width(7)) comparator_22 (.a(inst[31:25]), .b(7'b0100000), .eq(comparator_22_eq));  // open: gt, lt
  Comparator #(.width(7)) comparator_23 (.a(inst[6:0]), .b(7'b0000011), .eq(comparator_23_eq));  // open: gt, lt
  Comparator #(.width(3)) comparator_24 (.a(inst[14:12]), .b(3'b000), .eq(comparator_24_eq));  // open: gt, lt
  Comparator #(.width(7)) comparator_25 (.a(inst[6:0]), .b(7'b0000011), .eq(comparator_25_eq));  // open: gt, lt
  Comparator #(.width(3)) comparator_26 (.a(inst[14:12]), .b(3'b001), .eq(comparator_26_eq));  // open: gt, lt
  Comparator #(.width(7)) comparator_27 (.a(inst[6:0]), .b(7'b0000011), .eq(comparator_27_eq));  // open: gt, lt
  Comparator #(.width(3)) comparator_28 (.a(inst[14:12]), .b(3'b010), .eq(comparator_28_eq));  // open: gt, lt
  Comparator #(.width(7)) comparator_29 (.a(inst[6:0]), .b(7'b0010011), .eq(comparator_29_eq));  // open: gt, lt
  Comparator #(.width(3)) comparator_30 (.a(inst[14:12]), .b(3'b000), .eq(comparator_30_eq));  // open: gt, lt
  Comparator #(.width(7)) comparator_31 (.a(inst[6:0]), .b(7'b0010011), .eq(comparator_31_eq));  // open: gt, lt
  Comparator #(.width(3)) comparator_32 (.a(inst[14:12]), .b(3'b001), .eq(comparator_32_eq));  // open: gt, lt
  Comparator #(.width(7)) comparator_33 (.a(inst[31:25]), .b({7{1'b0}}), .eq(comparator_33_eq));  // open: gt, lt
  Comparator #(.width(7)) comparator_34 (.a(inst[6:0]), .b(7'b0010011), .eq(comparator_34_eq));  // open: gt, lt
  Comparator #(.width(3)) comparator_35 (.a(inst[14:12]), .b(3'b010), .eq(comparator_35_eq));  // open: gt, lt
  Comparator #(.width(7)) comparator_36 (.a(inst[6:0]), .b(7'b0100011), .eq(comparator_36_eq));  // open: gt, lt
  Comparator #(.width(3)) comparator_37 (.a(inst[14:12]), .b(3'b000), .eq(comparator_37_eq));  // open: gt, lt
  Comparator #(.width(7)) comparator_38 (.a(inst[6:0]), .b(7'b0100011), .eq(comparator_38_eq));  // open: gt, lt
  Comparator #(.width(3)) comparator_39 (.a(inst[14:12]), .b(3'b001), .eq(comparator_39_eq));  // open: gt, lt
  Comparator #(.width(7)) comparator_40 (.a(inst[6:0]), .b(7'b0100011), .eq(comparator_40_eq));  // open: gt, lt
  Comparator #(.width(3)) comparator_41 (.a(inst[14:12]), .b(3'b010), .eq(comparator_41_eq));  // open: gt, lt
  Comparator #(.width(7)) comparator_42 (.a(inst[6:0]), .b(7'b1100011), .eq(comparator_42_eq));  // open: gt, lt
  Comparator #(.width(3)) comparator_43 (.a(inst[14:12]), .b(3'b000), .eq(comparator_43_eq));  // open: gt, lt
  Comparator #(.width(7)) comparator_44 (.a(inst[6:0]), .b(7'b1100011), .eq(comparator_44_eq));  // open: gt, lt
  Comparator #(.width(3)) comparator_45 (.a(inst[14:12]), .b(3'b001), .eq(comparator_45_eq));  // open: gt, lt
  Comparator #(.width(7)) comparator_46 (.a(inst[6:0]), .b(7'b1100011), .eq(comparator_46_eq));  // open: gt, lt
  Comparator #(.width(3)) comparator_47 (.a(inst[14:12]), .b(3'b100), .eq(comparator_47_eq));  // open: gt, lt
  Multiplexer #(.enable("false")) multiplexer_14 (
    .in0(multiplexer_8_out), .in1(1'b0), .out(multiplexer_14_out), .sel(S_Type));
  Multiplexer #(.enable("false")) multiplexer_15 (
    .in0(multiplexer_9_out), .in1(1'b1), .out(multiplexer_15_out), .sel(UJ_Type));
  Multiplexer #(.enable("false"), .width(3)) multiplexer_16 (
    .in0(multiplexer_11_out), .in1(3'b010), .out(multiplexer_16_out), .sel(SB_Type));
  Multiplexer #(.enable("false"), .width(4)) multiplexer_17 (
    .in0(multiplexer_13_out), .in1(4'b0010), .out(multiplexer_17_out), .sel(alu_or));
  Multiplexer #(.enable("false")) multiplexer_18 (
    .in0(multiplexer_14_out), .in1(1'b1), .out(multiplexer_18_out), .sel(SB_Type));
  Multiplexer #(.enable("false"), .width(4)) multiplexer_19 (
    .in0(4'b0000), .in1(multiplexer_3_out), .out(MemRW), .sel(S_Type));
  Multiplexer #(.enable("false")) multiplexer_20 (.in0(multiplexer_15_out), .in1(1'b1), .out(RegWEn), .sel(U_Type));
  Multiplexer #(.enable("false"), .width(2)) multiplexer_21 (
    .in0(multiplexer_12_out), .in1(2'b00), .out(multiplexer_21_out), .sel(I_0x67));
  Multiplexer #(.enable("false"), .width(3)) multiplexer_22 (
    .in0(multiplexer_16_out), .in1(3'b011), .out(multiplexer_22_out), .sel(U_Type));
  Multiplexer #(.enable("false"), .width(4)) multiplexer_23 (
    .in0(multiplexer_17_out), .in1(4'b0011), .out(multiplexer_23_out), .sel(alu_xor));
  and and_7 (Inst_add, and_1_out, comparator_11_eq, comparator_12_eq);
  and and_8 (Inst_and, and_2_out, comparator_13_eq, comparator_14_eq);
  and and_9 (Inst_or, and_3_out, comparator_15_eq, comparator_16_eq);
  and and_10 (Inst_xor, and_4_out, comparator_17_eq, comparator_18_eq);
  and and_11 (Inst_srl, and_5_out, comparator_19_eq, comparator_20_eq);
  and and_12 (Inst_sra, and_6_out, comparator_21_eq, comparator_22_eq);
  and and_13 (Inst_lb, comparator_23_eq, comparator_24_eq);
  and and_14 (Inst_lh, comparator_25_eq, comparator_26_eq);
  and and_15 (Inst_lw, comparator_27_eq, comparator_28_eq);
  and and_16 (Inst_addi, comparator_29_eq, comparator_30_eq);
  and and_17 (Inst_slli, comparator_31_eq, comparator_32_eq, comparator_33_eq);
  and and_18 (Inst_slti, comparator_34_eq, comparator_35_eq);
  and and_19 (Inst_sb, comparator_36_eq, comparator_37_eq);
  and and_20 (Inst_sh, comparator_38_eq, comparator_39_eq);
  and and_21 (Inst_sw, comparator_40_eq, comparator_41_eq);
  and and_22 (Inst_beq, comparator_42_eq, comparator_43_eq);
  and and_23 (Inst_bne, comparator_44_eq, comparator_45_eq);
  and and_24 (Inst_blt, comparator_46_eq, comparator_47_eq);
  Multiplexer #(.enable("false"), .width(4)) multiplexer_24 (
    .in0(multiplexer_23_out), .in1(4'b0100), .out(multiplexer_24_out), .sel(alu_srl));
  Multiplexer #(.enable("false")) multiplexer_25 (
    .in0(multiplexer_18_out), .in1(1'b1), .out(multiplexer_25_out), .sel(UJ_Type));
  and and_25 (BrUn, inst[13], SB_Type);
  Multiplexer #(.enable("false"), .width(2)) multiplexer_26 (
    .in0(multiplexer_21_out), .in1(2'b00), .out(multiplexer_26_out), .sel(UJ_Type));
  Multiplexer #(.enable("false"), .width(3)) multiplexer_27 (
    .in0(multiplexer_22_out), .in1(3'b110), .out(ImmSel), .sel(UJ_Type));
  Multiplexer #(.enable("false"), .width(4)) multiplexer_28 (
    .in0(multiplexer_24_out), .in1(4'b0101), .out(multiplexer_28_out), .sel(alu_sra));
  Multiplexer #(.enable("false")) multiplexer_29 (.in0(multiplexer_25_out), .in1(1'b1), .out(ASel), .sel(U_Type));
  Multiplexer #(.enable("false"), .width(2)) multiplexer_30 (
    .in0(multiplexer_26_out), .in1(2'b01), .out(WBSel), .sel(U_Type));
  Multiplexer #(.enable("false"), .width(4)) multiplexer_31 (
    .in0(multiplexer_28_out), .in1(4'b0110), .out(multiplexer_31_out), .sel(alu_sll));
  Multiplexer #(.enable("false"), .width(4)) multiplexer_32 (
    .in0(multiplexer_31_out), .in1(4'b0111), .out(multiplexer_32_out), .sel(alu_slt));
  Multiplexer #(.enable("false"), .width(4)) multiplexer_33 (
    .in0(multiplexer_32_out), .in1(4'b1010), .out(multiplexer_33_out), .sel(alu_mul));
  and and_26 (and_26_out, R_Type, 1'b1);
  Comparator #(.width(3)) comparator_48 (.a(inst[14:12]), .b(3'b001), .eq(comparator_48_eq));  // open: gt, lt
  Comparator #(.width(7)) comparator_49 (.a(inst[31:25]), .b({7{1'b0}}), .eq(comparator_49_eq));  // open: gt, lt
  and and_27 (and_27_out, R_Type, 1'b1);
  Comparator #(.width(3)) comparator_50 (.a(inst[14:12]), .b(3'b010), .eq(comparator_50_eq));  // open: gt, lt
  Comparator #(.width(7)) comparator_51 (.a(inst[31:25]), .b({7{1'b0}}), .eq(comparator_51_eq));  // open: gt, lt
  and and_28 (and_28_out, R_Type, 1'b1);
  Comparator #(.width(3)) comparator_52 (.a(inst[14:12]), .b(3'b000), .eq(comparator_52_eq));  // open: gt, lt
  Comparator #(.width(7)) comparator_53 (.a(inst[31:25]), .b(7'b0000001), .eq(comparator_53_eq));  // open: gt, lt
  and and_29 (and_29_out, R_Type, 1'b1);
  Comparator #(.width(3)) comparator_54 (.a(inst[14:12]), .b(3'b011), .eq(comparator_54_eq));  // open: gt, lt
  Comparator #(.width(7)) comparator_55 (.a(inst[31:25]), .b(7'b0000001), .eq(comparator_55_eq));  // open: gt, lt
  and and_30 (and_30_out, R_Type, 1'b1);
  Comparator #(.width(3)) comparator_56 (.a(inst[14:12]), .b(3'b000), .eq(comparator_56_eq));  // open: gt, lt
  Comparator #(.width(7)) comparator_57 (.a(inst[31:25]), .b(7'b0100000), .eq(comparator_57_eq));  // open: gt, lt
  and and_31 (and_31_out, R_Type, 1'b1);
  Comparator #(.width(3)) comparator_58 (.a(inst[14:12]), .b(3'b001), .eq(comparator_58_eq));  // open: gt, lt
  Comparator #(.width(7)) comparator_59 (.a(inst[31:25]), .b(7'b0000001), .eq(comparator_59_eq));  // open: gt, lt
  Comparator #(.width(7)) comparator_60 (.a(inst[6:0]), .b(7'b0010011), .eq(comparator_60_eq));  // open: gt, lt
  Comparator #(.width(3)) comparator_61 (.a(inst[14:12]), .b(3'b100), .eq(comparator_61_eq));  // open: gt, lt
  Comparator #(.width(7)) comparator_62 (.a(inst[6:0]), .b(7'b0010011), .eq(comparator_62_eq));  // open: gt, lt
  Comparator #(.width(3)) comparator_63 (.a(inst[14:12]), .b(3'b101), .eq(comparator_63_eq));  // open: gt, lt
  Comparator #(.width(7)) comparator_64 (.a(inst[31:25]), .b({7{1'b0}}), .eq(comparator_64_eq));  // open: gt, lt
  Comparator #(.width(7)) comparator_65 (.a(inst[6:0]), .b(7'b0010111), .eq(Inst_auipc));  // open: gt, lt
  Comparator #(.width(7)) comparator_66 (.a(inst[6:0]), .b(7'b0110111), .eq(alu_bsel));  // open: gt, lt
  Comparator #(.width(7)) comparator_67 (.a(inst[6:0]), .b(7'b1101111), .eq(Inst_jal));  // open: gt, lt
  Comparator #(.width(7)) comparator_68 (.a(inst[6:0]), .b(7'b1100011), .eq(comparator_68_eq));  // open: gt, lt
  Comparator #(.width(3)) comparator_69 (.a(inst[14:12]), .b(3'b101), .eq(comparator_69_eq));  // open: gt, lt
  Comparator #(.width(7)) comparator_70 (.a(inst[6:0]), .b(7'b1100011), .eq(comparator_70_eq));  // open: gt, lt
  Comparator #(.width(3)) comparator_71 (.a(inst[14:12]), .b(3'b110), .eq(comparator_71_eq));  // open: gt, lt
  Comparator #(.width(7)) comparator_72 (.a(inst[6:0]), .b(7'b1100011), .eq(comparator_72_eq));  // open: gt, lt
  Comparator #(.width(3)) comparator_73 (.a(inst[14:12]), .b(3'b111), .eq(comparator_73_eq));  // open: gt, lt
  Comparator #(.width(7)) comparator_74 (.a(inst[6:0]), .b(7'b0010011), .eq(comparator_74_eq));  // open: gt, lt
  Comparator #(.width(3)) comparator_75 (.a(inst[14:12]), .b(3'b101), .eq(comparator_75_eq));  // open: gt, lt
  Comparator #(.width(7)) comparator_76 (.a(inst[31:25]), .b(7'b0100000), .eq(comparator_76_eq));  // open: gt, lt
  Comparator #(.width(7)) comparator_77 (.a(inst[6:0]), .b(7'b0010011), .eq(comparator_77_eq));  // open: gt, lt
  Comparator #(.width(3)) comparator_78 (.a(inst[14:12]), .b(3'b110), .eq(comparator_78_eq));  // open: gt, lt
  Comparator #(.width(7)) comparator_79 (.a(inst[6:0]), .b(7'b0010011), .eq(comparator_79_eq));  // open: gt, lt
  Comparator #(.width(3)) comparator_80 (.a(inst[14:12]), .b(3'b111), .eq(comparator_80_eq));  // open: gt, lt
  Multiplexer #(.enable("false"), .width(4)) multiplexer_34 (
    .in0(multiplexer_33_out), .in1(4'b1011), .out(multiplexer_34_out), .sel(alu_mulhu));
  and and_32 (Inst_sll, and_26_out, comparator_48_eq, comparator_49_eq);
  and and_33 (Inst_slt, and_27_out, comparator_50_eq, comparator_51_eq);
  and and_34 (alu_mul, and_28_out, comparator_52_eq, comparator_53_eq);
  and and_35 (alu_mulhu, and_29_out, comparator_54_eq, comparator_55_eq);
  and and_36 (alu_sub, and_30_out, comparator_56_eq, comparator_57_eq);
  and and_37 (alu_mulh, and_31_out, comparator_58_eq, comparator_59_eq);
  and and_38 (Inst_xori, comparator_60_eq, comparator_61_eq);
  and and_39 (Inst_bge, comparator_68_eq, comparator_69_eq);
  and and_40 (Inst_bltu, comparator_70_eq, comparator_71_eq);
  and and_41 (Inst_bgeu, comparator_72_eq, comparator_73_eq);
  Multiplexer #(.enable("false")) multiplexer_35 (.in0(1'b0), .in1(1'b1), .out(multiplexer_35_out), .sel(Inst_beq));
  Multiplexer #(.enable("false")) multiplexer_36 (.in0(1'b0), .in1(1'b1), .out(multiplexer_36_out), .sel(Inst_bne));
  Multiplexer #(.enable("false")) multiplexer_37 (.in0(1'b0), .in1(1'b1), .out(multiplexer_37_out), .sel(Inst_blt));
  Multiplexer #(.enable("false")) multiplexer_38 (.in0(1'b0), .in1(1'b1), .out(multiplexer_38_out), .sel(Inst_bge));
  Multiplexer #(.enable("false")) multiplexer_39 (.in0(1'b0), .in1(1'b1), .out(multiplexer_39_out), .sel(Inst_bltu));
  Multiplexer #(.enable("false")) multiplexer_40 (.in0(1'b0), .in1(1'b1), .out(multiplexer_40_out), .sel(Inst_bgeu));
  Multiplexer #(.enable("false"), .width(4)) multiplexer_41 (
    .in0(multiplexer_34_out), .in1(4'b1100), .out(multiplexer_41_out), .sel(alu_sub));
  and and_42 (Inst_srli, comparator_62_eq, comparator_63_eq, comparator_64_eq);
  and and_43 (Inst_srai, comparator_74_eq, comparator_75_eq, comparator_76_eq);
  and and_44 (Inst_ori, comparator_77_eq, comparator_78_eq);
  and and_45 (Inst_andi, comparator_79_eq, comparator_80_eq);
  Multiplexer #(.enable("false"), .width(4)) multiplexer_42 (
    .in0(multiplexer_41_out), .in1(4'b1101), .out(multiplexer_42_out), .sel(alu_bsel));
  not not_1 (not_1_out, BrEq);
  not not_2 (not_2_out, BrLt);
  not not_3 (not_3_out, BrLt);
  Multiplexer #(.enable("false"), .width(4)) multiplexer_43 (
    .in0(multiplexer_42_out), .in1(4'b1110), .out(ALUSel), .sel(alu_mulh));
  and and_46 (and_46_out, multiplexer_35_out, BrEq);
  and and_47 (and_47_out, not_1_out, multiplexer_36_out);
  and and_48 (and_48_out, multiplexer_37_out, BrLt);
  and and_49 (and_49_out, not_2_out, multiplexer_38_out);
  and and_50 (and_50_out, multiplexer_39_out, BrLt);
  and and_51 (and_51_out, not_3_out, multiplexer_40_out);
  or or_11 (CSRWen, CSRSel, Inst_csrwi);
  Comparator #(.width(7)) comparator_81 (.a(inst[6:0]), .b(7'b1100111), .eq(comparator_81_eq));  // open: gt, lt
  Comparator #(.width(3)) comparator_82 (.a(inst[14:12]), .b(3'b000), .eq(comparator_82_eq));  // open: gt, lt
  Comparator #(.width(7)) comparator_83 (.a(inst[6:0]), .b(7'b1110011), .eq(comparator_83_eq));  // open: gt, lt
  Comparator #(.width(3)) comparator_84 (.a(inst[14:12]), .b(3'b001), .eq(comparator_84_eq));  // open: gt, lt
  Comparator #(.width(7)) comparator_85 (.a(inst[6:0]), .b(7'b1110011), .eq(comparator_85_eq));  // open: gt, lt
  Comparator #(.width(3)) comparator_86 (.a(inst[14:12]), .b(3'b101), .eq(comparator_86_eq));  // open: gt, lt
  and and_52 (Inst_jalr, comparator_81_eq, comparator_82_eq);
  and and_53 (CSRSel, comparator_83_eq, comparator_84_eq);
  and and_54 (Inst_csrwi, comparator_85_eq, comparator_86_eq);
  or or_12 (PCSel, Inst_jalr, and_46_out, and_47_out, and_48_out, and_49_out, and_50_out, and_51_out, Inst_jal);

  // Other names for the same wires on the sheet: Inst_lui = alu_bsel; Inst_mul = alu_mul; Inst_mulh = alu_mulh;
  //   Inst_mulhu = alu_mulhu; Inst_sub = alu_sub; opcode[6:0] = inst[6:0]; rd[4:0] = inst[11:7];
  //   funct3[2:0] = inst[14:12]; rs1[4:0] = inst[19:15]; rs2[4:0] = inst[24:20]; funct7[6:0] = inst[31:25];
  //   Inst_csrw = CSRSel

  // Notes on the sheet:
  //   INPUTS to your circuit
  //   DON'T CHANGE THE LOCATIONS OF THE INPUTS AND OUTPUTS!
  //   OUTPUT from your circuit
  //   ASel
  //   BSel
  //   MemRW
  //   RegWEn
  //   ImmSel
  //   ALUSel
  //   R-type Instruction 
  //   I-type Instruction 
  //   S-type Instruction 
  //   SB-type Instruction 
  //   WBSel(I_0x73 is not implemented )
  //   BrUn
  //   U-type Instruction 
  //   UJ-type Instruction 
  //   PCSel
  //   CSR
endmodule
