// Logisim project cpu.circ as structural Verilog: 1 circuit, main circuit cpu
module cpu (
  input  clk,
  input  [31:0] INSTRUCTION,
  input  [31:0] READ_DATA,
  output [31:0] WRITE_ADDRESS,
  output [31:0] PROGRAM_COUNTER,
  output [31:0] ra,
  output [31:0] sp,
  output [31:0] t0,
  output [31:0] t1,
  output [31:0] t2,
  output [31:0] s0,
  output [31:0] s1,
  output [31:0] a0,
  output [31:0] tohost,
  output [3:0] WRITE_ENABLE,
  output [31:0] WRITE_DATA
);

  wire Aselec, BranEq, BranLt, BranUn, Bselec, CSRSele, CSRWriEn, PcSel, regWriEn;
  wire [1:0] bit_extender_2_out, WBSele;
  wire [2:0] funct3, ImmeSel;
  wire [3:0] AluSel;
  wire [4:0] bit_extender_3_out, CSRuimm, shifter_1_out;
  wire [7:0] bit_extender_4_out;
  wire [11:0] CSRSource, INSTRUCTION_OUTPUT;
  wire [15:0] bit_extender_5_out;
  wire [31:0] adder_1_out, adder_2_out, Alu_inA, Alu_inB, bit_extender_1_out, bit_extender_6_out,
       bit_extender_7_out, CSRData, DATA_PROCESSED, imme_output, multiplexer_1_out, multiplexer_2_out,
       PC_Stage2, read_data_1, shifter_2_out, WriteData;

  Adder #(.width(32)) adder_1 (.a(PROGRAM_COUNTER), .b(32'h4), .out(adder_1_out));  // open: cin, cout
  Multiplexer #(.enable("false"), .width(32)) multiplexer_1 (
    .in0(adder_1_out), .in1(WRITE_ADDRESS), .out(multiplexer_1_out), .sel(PcSel));
  Multiplexer #(.enable("false"), .width(32)) multiplexer_2 (
    .in0(INSTRUCTION), .in1(32'h13), .out(multiplexer_2_out), .sel(PcSel));
  Register #(.width(32)) PC (.D(multiplexer_1_out), .clk(clk), .Q(PROGRAM_COUNTER));  // open: en, clr
  Register #(.width(32)) register_1 (
    .D(multiplexer_2_out), .clk(clk), .Q({CSRSource, CSRuimm, funct3, INSTRUCTION_OUTPUT}));  // open: en, clr
  control_logic control_logic_1 (
    .CSRWen(CSRWriEn), .PCSel(PcSel), .RegWEn(regWriEn), .ImmSel(ImmeSel), .BrUn(BranUn), .ASel(Aselec),
    .BSel(Bselec), .ALUSel(AluSel), .MemRW(WRITE_ENABLE), .WBSel(WBSele), .CSRSel(CSRSele),
    .inst({CSRSource, CSRuimm, funct3, INSTRUCTION_OUTPUT}), .BrEq(BranEq), .BrLt(BranLt));
  Register #(.width(32)) register_2 (.D(PROGRAM_COUNTER), .clk(clk), .Q(PC_Stage2));  // open: en, clr
  regfile regfile_1 (
    .rs1(CSRuimm), .rs2(CSRSource[4:0]), .rd(INSTRUCTION_OUTPUT[11:7]), .Write_Data(WriteData),
    .RegWEn(regWriEn), .clk(clk), .ra(ra), .sp(sp), .t0(t0), .t1(t1), .t2(t2), .s0(s0), .s1(s1), .a0(a0),
    .Read_Data_1(read_data_1), .Read_Data_2(WRITE_DATA));
  imm_gen imm_gen_1 (.inst({CSRSource, CSRuimm, funct3, INSTRUCTION_OUTPUT}), .ImmSel(ImmeSel), .imm(imme_output));
  Multiplexer #(.enable("false"), .width(32)) multiplexer_3 (
    .in0(read_data_1), .in1(PC_Stage2), .out(Alu_inA), .sel(Aselec));
  Multiplexer #(.enable("false"), .width(32)) multiplexer_4 (
    .in0(WRITE_DATA), .in1(imme_output), .out(Alu_inB), .sel(Bselec));
  alu alu_1 (.Result(WRITE_ADDRESS), .A(Alu_inA), .B(Alu_inB), .ALUSel(AluSel));
  assign bit_extender_1_out = {{27{1'b0}}, CSRuimm};  // Bit_Extender bit_extender_1
  Multiplexer #(.enable("false"), .width(32)) multiplexer_5 (
    .in0(bit_extender_1_out), .in1(read_data_1), .out(CSRData), .sel(CSRSele));
  branch_comp branch_comp_1 (.rs1(read_data_1), .rs2(WRITE_DATA), .BrUn(BranUn), .BrEq(BranEq), .BrLt(BranLt));
  csr csr_1 (.CSR_address(CSRSource), .CSR_din(CSRData), .CSR_WE(CSRWriEn), .clk(clk), .tohost(tohost));
  Bit_Extender #(.in_width(32), .out_width(2), .\type ("zero")) bit_extender_2 (
    .in(WRITE_ADDRESS), .out(bit_extender_2_out));
  assign bit_extender_3_out = {{3{1'b0}}, bit_extender_2_out};  // Bit_Extender bit_extender_3
  Shifter #(.width(5)) shifter_1 (.in(bit_extender_3_out), .\dist (3'b011), .out(shifter_1_out));
  Shifter #(.shift("lr"), .width(32)) shifter_2 (.in(READ_DATA), .\dist (shifter_1_out), .out(shifter_2_out));
  Bit_Extender #(.in_width(32), .out_width(8), .\type ("zero")) bit_extender_4 (
    .in(shifter_2_out), .out(bit_extender_4_out));
  Bit_Extender #(.in_width(32), .\type ("zero")) bit_extender_5 (.in(shifter_2_out), .out(bit_extender_5_out));
  Adder #(.width(32)) adder_2 (.a(PC_Stage2), .b(32'h4), .out(adder_2_out));  // open: cin, cout
  assign bit_extender_6_out = {{24{bit_extender_4_out[7]}}, bit_extender_4_out};  // Bit_Extender bit_extender_6
  assign bit_extender_7_out = {{16{bit_extender_5_out[15]}}, bit_extender_5_out};  // Bit_Extender bit_extender_7
  Multiplexer #(.enable("false"), .select(2), .width(32)) multiplexer_6 (
    .in0(bit_extender_6_out), .in1(bit_extender_7_out), .in2(READ_DATA), .out(DATA_PROCESSED),
    .sel(funct3[1:0]));  // open: in3
  Multiplexer #(.enable("false"), .select(2), .width(32)) multiplexer_7 (
    .in0(adder_2_out), .in1(WRITE_ADDRESS), .in2(DATA_PROCESSED), .out(WriteData), .sel(WBSele));  // open: in3

  // Other names for the same wires on the sheet: Alu_Output[31:0] = WRITE_ADDRESS;
  //   opcode[6:0] = INSTRUCTION_OUTPUT[6:0]; rd[4:0] = INSTRUCTION_OUTPUT[11:7];
  //   INSTRUCTION_OUTPUT[31:12] = {CSRSource, CSRuimm, funct3}; rs1[4:0] = CSRuimm; rs2[4:0] = CSRSource[4:0];
  //   funct7[6:0] = CSRSource[11:5]; MemRorW[3:0] = WRITE_ENABLE; read_data_2[31:0] = WRITE_DATA

  // Notes on the sheet:
  //   Instruction Fetch
  //   Output to IMEM
  //   IMEM (do **NOT** move this)
  //   Inputs from IMEM
  //   Instruction Decode
  //   Inputs/Outputs for testing. Do **NOT** move these.
  //   Execute
  //   Outputs To DMEM
  //   DMEM (do **NOT** move this)
  //   Memory
  //   Inputs From DMEM
  //   READ_DATA Preprocessing
  //   Write Back 
endmodule
