// Logisim project imm_gen.circ as structural Verilog: 1 circuit, main circuit imm_gen
module imm_gen (
  input  [31:0] inst,
  input  [2:0] ImmSel,
  output [31:0] imm
);

  wire [31:0] I_Type_Output, S_Type_Output, SB_Type_Output, UJ_Type_Output;

  assign I_Type_Output = {{20{inst[31]}}, inst[31:20]};  // Bit_Extender bit_extender_1
  assign S_Type_Output = {{20{inst[31]}}, {inst[31:25], inst[11:7]}};  // Bit_Extender bit_extender_2
  assign SB_Type_Output = {{19{inst[31]}}, {inst[31], inst[7], inst[30:25], inst[11:8], 1'b0}};  // Bit_Extender bit_extender_3
  assign UJ_Type_Output = {{11{inst[31]}}, {inst[31], inst[19:12], inst[20], inst[30:21], 1'b0}};  // Bit_Extender bit_extender_4
  Multiplexer #(.enable("false"), .select(3), .width(32)) multiplexer_1 (
    .in0({32{1'b0}}), .in1(S_Type_Output), .in2(SB_Type_Output), .in3({inst[31:12], {12{1'b0}}}),
    .in4({32{1'b0}}), .in5({32{1'b0}}), .in6(UJ_Type_Output), .in7(I_Type_Output), .out(imm), .sel(ImmSel));

  // Other names for the same wires on the sheet: imme_output[31:0] = imm; U_Type_Output[31:12] = inst[31:12]

  // Notes on the sheet:
  //   INPUTS to your circuit
  //   DON'T CHANGE THE LOCATIONS OF THE INPUTS AND OUTPUTS!
  //   OUTPUT from your circuit
endmodule
