// Logisim project regfile.circ as structural Verilog: 1 circuit, main circuit regfile
module regfile (
  input  [4:0] rs1,
  input  [4:0] rs2,
  input  [4:0] rd,
  input  [31:0] Write_Data,
  input  RegWEn,
  input  clk,
  output [31:0] ra,
  output [31:0] sp,
  output [31:0] t0,
  output [31:0] t1,
  output [31:0] t2,
  output [31:0] s0,
  output [31:0] s1,
  output [31:0] a0,
  output [31:0] Read_Data_1,
  output [31:0] Read_Data_2
);

  wire clock_1_out, ra_W, x0_W, x2_W, x3_W, x4_W, x5_W, x6_W, x7_W, x8_W, x9_W, x10_W, x11_W, x12_W, x13_W,
       x14_W, x15_W, x16_W, x17_W, x18_W, x19_W, x20_W, x21_W, x22_W, x23_W, x24_W, x25_W, x26_W, x27_W,
       x28_W, x29_W, x30_W, x31_W;
  wire [31:0] x3, x4, x11, x12, x13, x14, x15, x16, x17, x18, x19, x20, x21, x22, x23, x24, x25, x26, x27,
       x28, x29, x30, x31;

  Clock clock_1 (.out(clock_1_out));
  Register #(.width(32)) x1 (.D(Write_Data), .en(ra_W), .clk(clock_1_out), .Q(ra));  // open: clr
  Register #(.width(32)) x2 (.D(Write_Data), .en(x2_W), .clk(clock_1_out), .Q(sp));  // open: clr
  Register #(.width(32)) register_1 (.D(Write_Data), .en(x3_W), .clk(clock_1_out), .Q(x3));  // open: clr
  Register #(.width(32)) register_2 (.D(Write_Data), .en(x4_W), .clk(clock_1_out), .Q(x4));  // open: clr
  Register #(.width(32)) register_3 (.D(Write_Data), .en(x5_W), .clk(clock_1_out), .Q(t0));  // open: clr
  Register #(.width(32)) register_4 (.D(Write_Data), .en(x6_W), .clk(clock_1_out), .Q(t1));  // open: clr
  Register #(.width(32)) register_5 (.D(Write_Data), .en(x7_W), .clk(clock_1_out), .Q(t2));  // open: clr
  Register #(.width(32)) register_6 (.D(Write_Data), .en(x8_W), .clk(clock_1_out), .Q(s0));  // open: clr
  Register #(.width(32)) register_7 (.D(Write_Data), .en(x9_W), .clk(clock_1_out), .Q(s1));  // open: clr
  Register #(.width(32)) register_8 (.D(Write_Data), .en(x10_W), .clk(clock_1_out), .Q(a0));  // open: clr
  Register #(.width(32)) register_9 (.D(Write_Data), .en(x11_W), .clk(clock_1_out), .Q(x11));  // open: clr
  Register #(.width(32)) register_10 (.D(Write_Data), .en(x12_W), .clk(clock_1_out), .Q(x12));  // open: clr
  Register #(.width(32)) register_11 (.D(Write_Data), .en(x13_W), .clk(clock_1_out), .Q(x13));  // open: clr
  Register #(.width(32)) register_12 (.D(Write_Data), .en(x14_W), .clk(clock_1_out), .Q(x14));  // open: clr
  Register #(.width(32)) register_13 (.D(Write_Data), .en(x15_W), .clk(clock_1_out), .Q(x15));  // open: clr
  Register #(.width(32)) register_14 (.D(Write_Data), .en(x16_W), .clk(clock_1_out), .Q(x16));  // open: clr
  Register #(.width(32)) register_15 (.D(Write_Data), .en(x17_W), .clk(clock_1_out), .Q(x17));  // open: clr
  Register #(.width(32)) register_16 (.D(Write_Data), .en(x18_W), .clk(clock_1_out), .Q(x18));  // open: clr
  Register #(.width(32)) register_17 (.D(Write_Data), .en(x19_W), .clk(clock_1_out), .Q(x19));  // open: clr
  Register #(.width(32)) register_18 (.D(Write_Data), .en(x20_W), .clk(clock_1_out), .Q(x20));  // open: clr
  Register #(.width(32)) register_19 (.D(Write_Data), .en(x21_W), .clk(clock_1_out), .Q(x21));  // open: clr
  Register #(.width(32)) register_20 (.D(Write_Data), .en(x22_W), .clk(clock_1_out), .Q(x22));  // open: clr
  Register #(.width(32)) register_21 (.D(Write_Data), .en(x23_W), .clk(clock_1_out), .Q(x23));  // open: clr
  Register #(.width(32)) register_22 (.D(Write_Data), .en(x24_W), .clk(clock_1_out), .Q(x24));  // open: clr
  Register #(.width(32)) register_23 (.D(Write_Data), .en(x25_W), .clk(clock_1_out), .Q(x25));  // open: clr
  Register #(.width(32)) register_24 (.D(Write_Data), .en(x26_W), .clk(clock_1_out), .Q(x26));  // open: clr
  Register #(.width(32)) register_25 (.D(Write_Data), .en(x27_W), .clk(clock_1_out), .Q(x27));  // open: clr
  Register #(.width(32)) register_26 (.D(Write_Data), .en(x28_W), .clk(clock_1_out), .Q(x28));  // open: clr
  Register #(.width(32)) register_27 (.D(Write_Data), .en(x29_W), .clk(clock_1_out), .Q(x29));  // open: clr
  Register #(.width(32)) register_28 (.D(Write_Data), .en(x30_W), .clk(clock_1_out), .Q(x30));  // open: clr
  Register #(.width(32)) register_29 (.D(Write_Data), .en(x31_W), .clk(clock_1_out), .Q(x31));  // open: clr
  Multiplexer #(.enable("false"), .select(5), .width(32)) multiplexer_1 (
    .in0({32{1'b0}}), .in1(ra), .in2(sp), .in3(x3), .in4(x4), .in5(t0), .in6(t1), .in7(t2), .in8(s0),
    .in9(s1), .in10(a0), .in11(x11), .in12(x12), .in13(x13), .in14(x14), .in15(x15), .in16(x16), .in17(x17),
    .in18(x18), .in19(x19), .in20(x20), .in21(x21), .in22(x22), .in23(x23), .in24(x24), .in25(x25),
    .in26(x26), .in27(x27), .in28(x28), .in29(x29), .in30(x30), .in31(x31), .out(Read_Data_1), .sel(rs1));
  Multiplexer #(.enable("false"), .select(5), .width(32)) multiplexer_2 (
    .in0({32{1'b0}}), .in1(ra), .in2(sp), .in3(x3), .in4(x4), .in5(t0), .in6(t1), .in7(t2), .in8(s0),
    .in9(s1), .in10(a0), .in11(x11), .in12(x12), .in13(x13), .in14(x14), .in15(x15), .in16(x16), .in17(x17),
    .in18(x18), .in19(x19), .in20(x20), .in21(x21), .in22(x22), .in23(x23), .in24(x24), .in25(x25),
    .in26(x26), .in27(x27), .in28(x28), .in29(x29), .in30(x30), .in31(x31), .out(Read_Data_2), .sel(rs2));
  Demultiplexer #(.enable("false"), .select(5)) demultiplexer_1 (
    .out0(x0_W), .out1(ra_W), .out2(x2_W), .out3(x3_W), .out4(x4_W), .out5(x5_W), .out6(x6_W), .out7(x7_W),
    .out8(x8_W), .out9(x9_W), .out10(x10_W), .out11(x11_W), .out12(x12_W), .out13(x13_W), .out14(x14_W),
    .out15(x15_W), .out16(x16_W), .out17(x17_W), .out18(x18_W), .out19(x19_W), .out20(x20_W), .out21(x21_W),
    .out22(x22_W), .out23(x23_W), .out24(x24_W), .out25(x25_W), .out26(x26_W), .out27(x27_W), .out28(x28_W),
    .out29(x29_W), .out30(x30_W), .out31(x31_W), .in(RegWEn), .sel(rd));

  // Other names for the same wires on the sheet: read_data1[31:0] = Read_Data_1; read_data2[31:0] = Read_Data_2;
  //   read_reg1[4:0] = rs1; read_reg2[4:0] = rs2; write_en = RegWEn; write_reg[4:0] = rd

  // Notes on the sheet:
  //   INPUTS to your circuit
  //   DON'T CHANGE THE LOCATIONS OF THE INPUTS AND OUTPUTS!
  //   These are DEBUG/TEST outputs from your circuit.
  //   OUTPUTS from your circuit
endmodule
